// Logisim project Logisim Project.circ as structural Verilog: 1 circuit, main circuit main
module main (
  input  f1,
  input  f0,
  input  A,
  input  B,
  output Output
);


  // Notes on the sheet:
  //   Christopher McDaniel
endmodule
